// Logisim project PROJECT.circ as structural Verilog: 9 circuits, main circuit main
module main (
  input  A3,
  input  A2,
  input  A1,
  input  A0,
  input  B3,
  input  B2,
  input  B1,
  input  B0,
  input  in_9,
  input  in_10,
  output out_11,
  output out_12,
  output out_13,
  output out_14,
  output out_15,
  output out_16,
  output out_17,
  output out_18
);

  allinone allinone_1 (
    .C1(in_9), .C0(in_10), .in_1(A3), .in_2(A2), .in_3(A1), .A0(A0), .in_5(B3), .in_6(B2), .in_7(B1),
    .B0(B0), .out_12(out_11), .out_13(out_12), .out_14(out_13), .out_15(out_14), .out_16(out_15),
    .out_17(out_16), .out_18(out_17), .out_11(out_18));

  // Notes on the sheet:
  //   00&01 multiplication
  //   10 addition
  //   11 substraction
  //   number a
  //   number b
endmodule

module Full_adder (
  input  in_1,
  input  in_2,
  input  in_3,
  output out_4,
  output out_5
);

  wire and_1_out, and_2_out, xor_1_out;

  xor xor_1 (xor_1_out, in_1, in_2);
  and and_1 (and_1_out, in_1, in_2);
  and and_2 (and_2_out, xor_1_out, in_3);
  xor xor_2 (out_4, xor_1_out, in_3);
  or or_1 (out_5, and_2_out, and_1_out);
endmodule

module _2LMultiplexer (
  input  in_1,
  input  in_2,
  input  in_3,
  output out_4
);

  wire and_1_out, and_2_out, not_1_out;

  not not_1 (not_1_out, in_3);
  and and_1 (and_1_out, in_1, not_1_out);
  and and_2 (and_2_out, in_3, in_2);
  or or_1 (out_4, and_1_out, and_2_out);
endmodule

module _4LMultiplexer (
  input  in_1,
  input  in_2,
  input  in_3,
  input  in_4,
  input  in_5,
  input  in_6,
  output out_7
);

  wire and_1_out, and_2_out, and_3_out, and_4_out, not_1_out, not_2_out, not_3_out, not_4_out;

  not not_1 (not_1_out, in_5);
  not not_2 (not_2_out, in_6);
  not not_3 (not_3_out, in_5);
  not not_4 (not_4_out, in_6);
  and and_1 (and_1_out, not_1_out, not_2_out, in_1);
  and and_2 (and_2_out, not_3_out, in_6, in_2);
  and and_3 (and_3_out, in_5, not_4_out, in_3);
  and and_4 (and_4_out, in_5, in_6, in_4);
  or or_1 (out_7, and_1_out, and_2_out, and_3_out, and_4_out);
endmodule

module ALU (
  input  in_1,
  input  in_2,
  input  in_3,
  input  in_4,
  input  in_5,
  output out_6,
  output out_7
);

  wire and_1_out, and_2_out, full_adder_1_out_4, n2lmultiplexer_1_out_4, not_1_out, or_1_out;

  _2LMultiplexer u_2lmultiplexer_1 (.in_1(in_3), .in_2(not_1_out), .out_4(n2lmultiplexer_1_out_4), .in_3(and_2_out));
  not not_1 (not_1_out, in_3);
  and and_1 (and_1_out, in_2, in_3);
  or or_1 (or_1_out, in_2, in_3);
  Full_adder full_adder_1 (
    .in_1(in_2), .in_2(n2lmultiplexer_1_out_4), .in_3(in_1), .out_4(full_adder_1_out_4), .out_5(out_7));
  and and_2 (and_2_out, in_5, in_4);
  _4LMultiplexer u_4lmultiplexer_1 (
    .in_1(and_1_out), .in_2(or_1_out), .in_3(full_adder_1_out_4), .in_4(full_adder_1_out_4), .out_7(out_6),
    .in_5(in_4), .in_6(in_5));
endmodule

module _4bit_add_sub (
  input  C1,
  input  C0,
  input  A0,
  input  A1,
  input  A2,
  input  A3,
  input  B0,
  input  B1,
  input  B2,
  input  B3,
  output out_11,
  output out_12,
  output out_13,
  output out_14,
  output out_15,
  output out_16,
  output out_17,
  output out_18
);

  wire alu_1_out_7, alu_2_out_7, alu_3_out_7, alu_4_out_7, alu_5_out_7, alu_6_out_7, alu_7_out_7, and_1_out;

  and and_1 (and_1_out, C1, C0);
  ALU alu_1 (.in_2(A0), .in_3(B0), .out_6(out_12), .out_7(alu_1_out_7), .in_1(and_1_out), .in_4(C1), .in_5(C0));
  ALU alu_2 (.in_2(A1), .in_3(B1), .out_6(out_11), .out_7(alu_2_out_7), .in_1(alu_1_out_7), .in_4(C1), .in_5(C0));
  ALU alu_3 (.in_2(A2), .in_3(B2), .out_6(out_18), .out_7(alu_3_out_7), .in_1(alu_2_out_7), .in_4(C1), .in_5(C0));
  ALU alu_4 (.in_2(A3), .in_3(B3), .out_6(out_17), .out_7(alu_4_out_7), .in_1(alu_3_out_7), .in_4(C1), .in_5(C0));
  ALU alu_5 (.in_2(A3), .in_3(B3), .out_6(out_16), .out_7(alu_5_out_7), .in_1(alu_4_out_7), .in_4(C1), .in_5(C0));
  ALU alu_6 (.in_2(A3), .in_3(B3), .out_6(out_15), .out_7(alu_6_out_7), .in_1(alu_5_out_7), .in_4(C1), .in_5(C0));
  ALU alu_7 (.in_2(A3), .in_3(B3), .out_6(out_14), .out_7(alu_7_out_7), .in_1(alu_6_out_7), .in_4(C1), .in_5(C0));
  ALU alu_8 (.in_2(A3), .in_3(B3), .out_6(out_13), .in_1(alu_7_out_7), .in_4(C1), .in_5(C0));  // open: out_7
endmodule

module _4bit_mul (
  input  A3,
  input  A2,
  input  A1,
  input  A0,
  input  B3,
  input  B2,
  input  B1,
  input  B0,
  output out_9,
  output out_10,
  output out_11,
  output out_12,
  output out_13,
  output out_14,
  output out_15,
  output out_16
);

  wire and_1_out, and_2_out, and_3_out, and_4_out, and_5_out, and_6_out, and_7_out, and_8_out, and_9_out,
       and_10_out, and_11_out, and_12_out, and_13_out, and_14_out, and_16_out, full_adder_2_out_5,
       half_adder_1_out_3, half_adder_2_out_3, half_adder_3_out_3, half_adder_4_out_3, half_adder_5_out_3,
       half_adder_6_out_3, half_adder_7_out_3, half_adder_7_out_4, half_adder_8_out_3, half_adder_8_out_4,
       half_adder_9_out_3, half_adder_9_out_4, half_adder_10_out_3, half_adder_10_out_4, half_adder_11_out_3,
       half_adder_11_out_4, half_adder_12_out_3, half_adder_12_out_4, half_adder_13_out_3,
       half_adder_13_out_4, half_adder_14_out_3, half_adder_14_out_4, half_adder_15_out_3,
       half_adder_15_out_4, half_adder_16_out_3, half_adder_16_out_4, half_adder_17_out_4,
       half_adder_18_out_3, half_adder_18_out_4, half_adder_19_out_3, half_adder_19_out_4,
       half_adder_20_out_3, half_adder_20_out_4, half_adder_21_out_3, half_adder_21_out_4,
       half_adder_22_out_4, half_adder_23_out_3, half_adder_23_out_4, half_adder_24_out_3,
       half_adder_24_out_4, half_adder_25_out_3, half_adder_25_out_4, half_adder_26_out_4,
       half_adder_27_out_3, half_adder_27_out_4, half_adder_28_out_3, half_adder_28_out_4,
       half_adder_29_out_4, half_adder_30_out_4, xor_1_out, xor_2_out, xor_3_out, xor_4_out, xor_5_out,
       xor_6_out, xor_7_out, xor_8_out, xor_9_out, xor_10_out, xor_11_out, xor_12_out, xor_13_out,
       xor_14_out, xor_15_out, xor_16_out, xor_17_out, xor_18_out, xor_19_out;

  Half_adder half_adder_1 (.in_1(and_13_out), .in_2(and_9_out), .out_3(half_adder_1_out_3));  // open: out_4
  Half_adder half_adder_2 (.in_1(half_adder_1_out_3), .in_2(and_6_out), .out_3(half_adder_2_out_3));  // open: out_4
  Half_adder half_adder_3 (.in_1(half_adder_2_out_3), .in_2(and_1_out), .out_3(half_adder_3_out_3));  // open: out_4
  Half_adder half_adder_4 (.in_1(half_adder_3_out_3), .in_2(and_1_out), .out_3(half_adder_4_out_3));  // open: out_4
  Half_adder half_adder_5 (.in_1(half_adder_4_out_3), .in_2(and_2_out), .out_3(half_adder_5_out_3));  // open: out_4
  Half_adder half_adder_6 (.in_1(half_adder_5_out_3), .in_2(and_4_out), .out_3(half_adder_6_out_3));  // open: out_4
  Full_adder full_adder_1 (
    .in_1(half_adder_6_out_3), .in_2(and_3_out), .in_3(xor_1_out), .out_4(out_14));  // open: out_5
  xor xor_1 (xor_1_out, full_adder_2_out_5, xor_2_out);
  xor xor_2 (xor_2_out, xor_3_out, half_adder_11_out_4);
  xor xor_3 (xor_3_out, xor_4_out, half_adder_9_out_4);
  Half_adder half_adder_7 (.in_1(and_13_out), .in_2(and_9_out), .out_3(half_adder_7_out_3), .out_4(half_adder_7_out_4));
  Half_adder half_adder_8 (
    .in_1(half_adder_7_out_3), .in_2(and_6_out), .out_3(half_adder_8_out_3), .out_4(half_adder_8_out_4));
  Half_adder half_adder_9 (
    .in_1(half_adder_8_out_3), .in_2(and_1_out), .out_3(half_adder_9_out_3), .out_4(half_adder_9_out_4));
  Half_adder half_adder_10 (
    .in_1(half_adder_9_out_3), .in_2(and_2_out), .out_3(half_adder_10_out_3), .out_4(half_adder_10_out_4));
  Half_adder half_adder_11 (
    .in_1(half_adder_10_out_3), .in_2(and_4_out), .out_3(half_adder_11_out_3), .out_4(half_adder_11_out_4));
  Full_adder full_adder_2 (
    .in_1(half_adder_11_out_3), .in_2(and_3_out), .in_3(xor_6_out), .out_4(out_15), .out_5(full_adder_2_out_5));
  xor xor_4 (xor_4_out, xor_5_out, half_adder_10_out_4);
  xor xor_5 (xor_5_out, half_adder_7_out_4, half_adder_8_out_4);
  xor xor_6 (xor_6_out, half_adder_17_out_4, xor_7_out);
  and and_1 (and_1_out, A3, B3);
  and and_2 (and_2_out, A2, B3);
  xor xor_7 (xor_7_out, half_adder_16_out_4, xor_8_out);
  and and_3 (and_3_out, A0, B3);
  and and_4 (and_4_out, A1, B3);
  Half_adder half_adder_12 (
    .in_1(and_13_out), .in_2(and_9_out), .out_3(half_adder_12_out_3), .out_4(half_adder_12_out_4));
  Half_adder half_adder_13 (
    .in_1(half_adder_12_out_3), .in_2(and_6_out), .out_3(half_adder_13_out_3), .out_4(half_adder_13_out_4));
  Half_adder half_adder_14 (
    .in_1(half_adder_13_out_3), .in_2(and_2_out), .out_3(half_adder_14_out_3), .out_4(half_adder_14_out_4));
  Half_adder half_adder_15 (
    .in_1(half_adder_14_out_3), .in_2(and_4_out), .out_3(half_adder_15_out_3), .out_4(half_adder_15_out_4));
  Half_adder half_adder_16 (
    .in_1(half_adder_15_out_3), .in_2(and_3_out), .out_3(half_adder_16_out_3), .out_4(half_adder_16_out_4));
  Half_adder half_adder_17 (.in_1(half_adder_16_out_3), .in_2(xor_11_out), .out_3(out_16), .out_4(half_adder_17_out_4));
  xor xor_8 (xor_8_out, xor_10_out, half_adder_15_out_4);
  xor xor_9 (xor_9_out, half_adder_12_out_4, half_adder_13_out_4);
  xor xor_10 (xor_10_out, xor_9_out, half_adder_14_out_4);
  and and_5 (and_5_out, A2, B2);
  and and_6 (and_6_out, A3, B2);
  xor xor_11 (xor_11_out, half_adder_21_out_4, xor_12_out);
  xor xor_12 (xor_12_out, half_adder_22_out_4, xor_13_out);
  and and_7 (and_7_out, A0, B2);
  and and_8 (and_8_out, A1, B2);
  Half_adder half_adder_18 (
    .in_1(and_13_out), .in_2(and_9_out), .out_3(half_adder_18_out_3), .out_4(half_adder_18_out_4));
  Half_adder half_adder_19 (
    .in_1(half_adder_18_out_3), .in_2(and_5_out), .out_3(half_adder_19_out_3), .out_4(half_adder_19_out_4));
  Half_adder half_adder_20 (
    .in_1(half_adder_19_out_3), .in_2(and_4_out), .out_3(half_adder_20_out_3), .out_4(half_adder_20_out_4));
  Half_adder half_adder_21 (
    .in_1(half_adder_20_out_3), .in_2(and_3_out), .out_3(half_adder_21_out_3), .out_4(half_adder_21_out_4));
  Half_adder half_adder_22 (.in_1(half_adder_21_out_3), .in_2(xor_14_out), .out_3(out_9), .out_4(half_adder_22_out_4));
  xor xor_13 (xor_13_out, xor_15_out, half_adder_20_out_4);
  and and_9 (and_9_out, A3, B1);
  xor xor_14 (xor_14_out, xor_16_out, half_adder_25_out_4);
  xor xor_15 (xor_15_out, half_adder_18_out_4, half_adder_19_out_4);
  and and_10 (and_10_out, A1, B1);
  and and_11 (and_11_out, A2, B1);
  Half_adder half_adder_23 (
    .in_1(and_13_out), .in_2(and_11_out), .out_3(half_adder_23_out_3), .out_4(half_adder_23_out_4));
  Half_adder half_adder_24 (
    .in_1(half_adder_23_out_3), .in_2(and_8_out), .out_3(half_adder_24_out_3), .out_4(half_adder_24_out_4));
  Half_adder half_adder_25 (
    .in_1(half_adder_24_out_3), .in_2(and_3_out), .out_3(half_adder_25_out_3), .out_4(half_adder_25_out_4));
  Half_adder half_adder_26 (.in_1(half_adder_25_out_3), .in_2(xor_18_out), .out_3(out_10), .out_4(half_adder_26_out_4));
  xor xor_16 (xor_16_out, half_adder_26_out_4, xor_17_out);
  xor xor_17 (xor_17_out, half_adder_23_out_4, half_adder_24_out_4);
  and and_12 (and_12_out, A0, B1);
  xor xor_18 (xor_18_out, half_adder_29_out_4, xor_19_out);
  and and_13 (and_13_out, A3, B0);
  and and_14 (and_14_out, A2, B0);
  Half_adder half_adder_27 (
    .in_1(and_14_out), .in_2(and_10_out), .out_3(half_adder_27_out_3), .out_4(half_adder_27_out_4));
  Half_adder half_adder_28 (
    .in_1(half_adder_27_out_3), .in_2(and_7_out), .out_3(half_adder_28_out_3), .out_4(half_adder_28_out_4));
  Half_adder half_adder_29 (
    .in_1(half_adder_28_out_3), .in_2(half_adder_30_out_4), .out_3(out_11), .out_4(half_adder_29_out_4));
  xor xor_19 (xor_19_out, half_adder_27_out_4, half_adder_28_out_4);
  and and_15 (out_13, A0, B0);
  and and_16 (and_16_out, A1, B0);
  Half_adder half_adder_30 (.in_1(and_16_out), .in_2(and_12_out), .out_3(out_12), .out_4(half_adder_30_out_4));
endmodule

module Half_adder (
  input  in_1,
  input  in_2,
  output out_3,
  output out_4
);

  xor xor_1 (out_3, in_1, in_2);
  and and_1 (out_4, in_1, in_2);
endmodule

module allinone (
  input  in_1,
  input  in_2,
  input  in_3,
  input  A0,
  input  in_5,
  input  in_6,
  input  in_7,
  input  B0,
  input  C1,
  input  C0,
  output out_11,
  output out_12,
  output out_13,
  output out_14,
  output out_15,
  output out_16,
  output out_17,
  output out_18
);

  wire n4bit_add_sub_1_out_11, n4bit_add_sub_1_out_12, n4bit_add_sub_1_out_13, n4bit_add_sub_1_out_14,
       n4bit_add_sub_1_out_15, n4bit_add_sub_1_out_16, n4bit_add_sub_1_out_17, n4bit_add_sub_1_out_18,
       n4bit_mul_1_out_9, n4bit_mul_1_out_10, n4bit_mul_1_out_11, n4bit_mul_1_out_12, n4bit_mul_1_out_13,
       n4bit_mul_1_out_14, n4bit_mul_1_out_15, n4bit_mul_1_out_16;

  _4LMultiplexer u_4lmultiplexer_1 (
    .in_1(n4bit_mul_1_out_14), .in_2(n4bit_mul_1_out_14), .in_3(n4bit_add_sub_1_out_13),
    .in_4(n4bit_add_sub_1_out_13), .out_7(out_12), .in_5(C1), .in_6(C0));
  _4LMultiplexer u_4lmultiplexer_2 (
    .in_1(n4bit_mul_1_out_15), .in_2(n4bit_mul_1_out_15), .in_3(n4bit_add_sub_1_out_14),
    .in_4(n4bit_add_sub_1_out_14), .out_7(out_13), .in_5(C1), .in_6(C0));
  _4LMultiplexer u_4lmultiplexer_3 (
    .in_1(n4bit_mul_1_out_16), .in_2(n4bit_mul_1_out_16), .in_3(n4bit_add_sub_1_out_15),
    .in_4(n4bit_add_sub_1_out_15), .out_7(out_14), .in_5(C1), .in_6(C0));
  _4LMultiplexer u_4lmultiplexer_4 (
    .in_1(n4bit_mul_1_out_9), .in_2(n4bit_mul_1_out_9), .in_3(n4bit_add_sub_1_out_16),
    .in_4(n4bit_add_sub_1_out_16), .out_7(out_15), .in_5(C1), .in_6(C0));
  _4bit_add_sub u_4bit_add_sub_1 (
    .A0(A0), .B0(B0), .A1(in_3), .B1(in_7), .A2(in_2), .B2(in_6), .A3(in_1), .B3(in_5), .C1(C1), .C0(C0),
    .out_17(n4bit_add_sub_1_out_17), .out_18(n4bit_add_sub_1_out_18), .out_11(n4bit_add_sub_1_out_11),
    .out_12(n4bit_add_sub_1_out_12), .out_16(n4bit_add_sub_1_out_16), .out_15(n4bit_add_sub_1_out_15),
    .out_14(n4bit_add_sub_1_out_14), .out_13(n4bit_add_sub_1_out_13));
  _4LMultiplexer u_4lmultiplexer_5 (
    .in_1(n4bit_mul_1_out_10), .in_2(n4bit_mul_1_out_10), .in_3(n4bit_add_sub_1_out_17),
    .in_4(n4bit_add_sub_1_out_17), .out_7(out_16), .in_5(C1), .in_6(C0));
  _4LMultiplexer u_4lmultiplexer_6 (
    .in_1(n4bit_mul_1_out_11), .in_2(n4bit_mul_1_out_11), .in_3(n4bit_add_sub_1_out_18),
    .in_4(n4bit_add_sub_1_out_18), .out_7(out_17), .in_5(C1), .in_6(C0));
  _4bit_mul u_4bit_mul_1 (
    .A3(in_1), .A2(in_2), .A1(in_3), .A0(A0), .out_14(n4bit_mul_1_out_14), .B3(in_5),
    .out_15(n4bit_mul_1_out_15), .B2(in_6), .out_16(n4bit_mul_1_out_16), .B1(in_7), .B0(B0),
    .out_9(n4bit_mul_1_out_9), .out_10(n4bit_mul_1_out_10), .out_11(n4bit_mul_1_out_11),
    .out_12(n4bit_mul_1_out_12), .out_13(n4bit_mul_1_out_13));
  _4LMultiplexer u_4lmultiplexer_7 (
    .in_1(n4bit_mul_1_out_12), .in_2(n4bit_mul_1_out_12), .in_3(n4bit_add_sub_1_out_11),
    .in_4(n4bit_add_sub_1_out_11), .out_7(out_18), .in_5(C1), .in_6(C0));
  _4LMultiplexer u_4lmultiplexer_8 (
    .in_1(n4bit_mul_1_out_13), .in_2(n4bit_mul_1_out_13), .in_3(n4bit_add_sub_1_out_12),
    .in_4(n4bit_add_sub_1_out_12), .out_7(out_11), .in_5(C1), .in_6(C0));
endmodule
